// Logisim project final_circuit.circ as structural Verilog
module main (
);

  wire clock_1_out, system_bus_1_buttons_e, system_bus_1_display_e, system_bus_1_ram_m;
  wire [2:0] system_bus_1_ram_ctrl;
  wire [3:0] system_bus_1_cpu_a_o, system_bus_1_ram_a;
  wire [5:0] stalwart_cpu_1_ext_ctrl;
  wire [6:0] display_handler_1_x1, display_handler_1_x10, display_handler_1_x100;
  wire [7:0] button_handler_1_o, ram_16x8_1_data_out, system_bus_1_cpu_d_o, system_bus_1_display;
  wire [9:0] button_7_out;

  Button button_1 (.out(button_7_out[2]));
  Button button_2 (.out(button_7_out[1]));
  Button button_3 (.out(button_7_out[4]));
  Button button_4 (.out(button_7_out[5]));
  Button button_5 (.out(button_7_out[7]));
  Button button_6 (.out(button_7_out[8]));
  Button button_7 (.out(button_7_out[0]));
  Clock clock_1 (.out(clock_1_out));
  ROM #(.addrWidth(4)) rom_1 ();  // open: addr, data
  Button button_8 (.out(button_7_out[3]));
  Button button_9 (.out(button_7_out[6]));
  Button button_10 (.out(button_7_out[9]));
  Button_Handler button_handler_1 (.O(button_handler_1_o), .CS(system_bus_1_buttons_e), .I(button_7_out));
  RAM_16x8 ram_16x8_1 (
    .Mode(system_bus_1_ram_m), .CLK(clock_1_out), .Data_in(ram_16x8_1_data_out),
    .Data_out(ram_16x8_1_data_out), .CPU_CTRL(system_bus_1_ram_ctrl), .Address(system_bus_1_ram_a));
  System_Bus system_bus_1 (
    .Display(system_bus_1_display), .CPU_CTRL(stalwart_cpu_1_ext_ctrl), .CPU_A_I(system_bus_1_cpu_a_o),
    .CPU_A_O(system_bus_1_cpu_a_o), .Buttons(button_handler_1_o), .RAM_A(system_bus_1_ram_a),
    .CPU_D_O(system_bus_1_cpu_d_o), .RAM_M(system_bus_1_ram_m), .Buttons_E(system_bus_1_buttons_e),
    .CPU_D_I(system_bus_1_cpu_d_o), .RAM_D_O(ram_16x8_1_data_out), .Display_E(system_bus_1_display_e),
    .RAM_D_I(ram_16x8_1_data_out), .RAM_CTRL(system_bus_1_ram_ctrl));
  Stalwart_CPU stalwart_cpu_1 (
    .EXT_CTRL(stalwart_cpu_1_ext_ctrl), .MBR_I(system_bus_1_cpu_d_o), .MAR_O(system_bus_1_cpu_a_o),
    .MBR_O(system_bus_1_cpu_d_o), .MAR_I(system_bus_1_cpu_a_o), .CLK(clock_1_out));
  _7_Segment_Display u_7_segment_display_1 (
    .g(display_handler_1_x100[0]), .f(display_handler_1_x100[1]), .a(display_handler_1_x100[2]),
    .b(display_handler_1_x100[3]), .e(display_handler_1_x100[6]), .d(display_handler_1_x100[5]),
    .c(display_handler_1_x100[4]));  // open: dp
  Display_Handler display_handler_1 (
    .x1(display_handler_1_x1), .x100(display_handler_1_x100), .x10(display_handler_1_x10),
    .I(system_bus_1_display), .IE(system_bus_1_display_e));
  _7_Segment_Display u_7_segment_display_2 (
    .g(display_handler_1_x10[0]), .f(display_handler_1_x10[1]), .a(display_handler_1_x10[2]),
    .b(display_handler_1_x10[3]), .e(display_handler_1_x10[6]), .d(display_handler_1_x10[5]),
    .c(display_handler_1_x10[4]));  // open: dp
  _7_Segment_Display u_7_segment_display_3 (
    .g(display_handler_1_x1[0]), .f(display_handler_1_x1[1]), .a(display_handler_1_x1[2]),
    .b(display_handler_1_x1[3]), .e(display_handler_1_x1[6]), .d(display_handler_1_x1[5]),
    .c(display_handler_1_x1[4]));  // open: dp

  // Notes on the sheet:
  //   contents of rom_1 (hex, n*v repeats v):
  //   4e 5d 34 3c 9a 6e 4f 1c 24 6f b0 4f 10 1
endmodule

module Button_Handler (
  input  [9:0] I,
  input  CS,
  output [7:0] O
);

  wire controlled_buffer_1_out, not_1_out, or_5_out;
  wire [3:0] byte_reg_1_o, or_4_out;
  wire [7:4] byte_reg_1_o_2;

  or or_1 (or_4_out[3], I[9], I[8]);
  or or_2 (or_4_out[2], I[7], I[6], I[5], I[4]);
  or or_3 (or_4_out[1], I[7], I[6], I[3], I[2]);
  or or_4 (or_4_out[0], I[9], I[7], I[5], I[3], I[1]);
  or or_5 (or_5_out, I[0], or_4_out[3], or_4_out[2], or_4_out[1], or_4_out[0]);
  assign controlled_buffer_1_out = not_1_out ? or_5_out : 1'bz;  // Controlled_Buffer controlled_buffer_1
  not not_1 (not_1_out, CS);
  Byte_Reg byte_reg_1 (
    .Chip_Select(1'b1), .Clock(controlled_buffer_1_out), .Mode_RW(controlled_buffer_1_out),
    .O({byte_reg_1_o_2, byte_reg_1_o}), .I({byte_reg_1_o, or_4_out}));
  assign O = CS ? {byte_reg_1_o_2, byte_reg_1_o} : 8'bz;  // Controlled_Buffer controlled_buffer_2
endmodule

module Display_Handler (
  input  [7:0] I,
  input  IE,
  output [6:0] x100,
  output [6:0] x10,
  output [6:0] x1
);

  wire controlled_buffer_1_out, or_1_out;
  wire [3:0] binary_to_bcd_1_binary1, binary_to_bcd_1_binary10, binary_to_bcd_1_binary100;
  wire [7:0] byte_reg_1_o;

  or or_1 (or_1_out, I[0], I[1], I[2], I[3], I[4], I[5], I[6], I[7]);
  assign controlled_buffer_1_out = IE ? or_1_out : 1'bz;  // Controlled_Buffer controlled_buffer_1
  Byte_Reg byte_reg_1 (
    .Chip_Select(1'b1), .Clock(controlled_buffer_1_out), .Mode_RW(controlled_buffer_1_out), .O(byte_reg_1_o),
    .I(I));
  Binary_to_BCD binary_to_bcd_1 (
    .BInaryInput(byte_reg_1_o), .Binary1(binary_to_bcd_1_binary1), .Binary10(binary_to_bcd_1_binary10),
    .Binary100(binary_to_bcd_1_binary100));
  BCD_to_7Segment bcd_to_7segment_1 (.in_1(binary_to_bcd_1_binary1), .out_2(x100));
  BCD_to_7Segment bcd_to_7segment_2 (.in_1(binary_to_bcd_1_binary10), .out_2(x10));
  BCD_to_7Segment bcd_to_7segment_3 (.in_1(binary_to_bcd_1_binary100), .out_2(x1));
  _7_Segment_Display u_7_segment_display_1 (
    .g(x100[0]), .f(x100[1]), .a(x100[2]), .b(x100[3]), .e(x100[6]), .d(x100[5]), .c(x100[4]));  // open: dp
  _7_Segment_Display u_7_segment_display_2 (
    .g(x10[0]), .f(x10[1]), .a(x10[2]), .b(x10[3]), .e(x10[6]), .d(x10[5]), .c(x10[4]));  // open: dp
  _7_Segment_Display u_7_segment_display_3 (
    .g(x1[0]), .f(x1[1]), .a(x1[2]), .b(x1[3]), .e(x1[6]), .d(x1[5]), .c(x1[4]));  // open: dp

  // Notes on the sheet:
  //   Segment order: GFABCDE
endmodule

module System_Bus (
  input  [3:0] CPU_A_I,
  input  [7:0] CPU_D_I,
  input  [7:0] RAM_D_I,
  input  [7:0] Buttons,
  input  [5:0] CPU_CTRL,
  output [3:0] CPU_A_O,
  output [3:0] RAM_A,
  output [7:0] CPU_D_O,
  output [7:0] RAM_D_O,
  output [7:0] Display,
  output [2:0] RAM_CTRL,
  output RAM_M,
  output Buttons_E,
  output Display_E
);


  assign Buttons_E = CPU_CTRL[4];
  assign CPU_A_O = CPU_A_I;
  assign CPU_D_I = Buttons;
  assign CPU_D_O = Buttons;
  assign Display = Buttons;
  assign Display_E = CPU_CTRL[5];
  assign RAM_A = CPU_A_I;
  assign RAM_CTRL = CPU_CTRL[2:0];
  assign RAM_D_I = Buttons;
  assign RAM_D_O = Buttons;
  assign RAM_M = CPU_CTRL[3];

  // Notes on the sheet:
  //   Address bus: 4 bits
  //   Data bus: 8 bits
  //   Control Bus: Set size as required
endmodule

module Stalwart_CPU (
  input  [3:0] MAR_I,
  input  [7:0] MBR_I,
  input  CLK,
  output [3:0] MAR_O,
  output [7:0] MBR_O,
  output [5:0] EXT_CTRL
);

  wire control_unit_1_alu_add_sub, control_unit_1_ir_cs, control_unit_1_ir_rw, control_unit_1_mar_cs,
       control_unit_1_mar_rw, control_unit_1_mbr_cs, control_unit_1_mbr_rw;
  wire [2:0] control_unit_1_ic_ctrl;
  wire [3:0] control_unit_1_alu_ctrl, control_unit_1_d0_rw;
  wire [7:0] D0_o, IR_o;

  Nibble_Reg MAR (
    .O(MAR_I), .Chip_Select(control_unit_1_mar_cs), .Mode_RW(control_unit_1_mar_rw), .Clock(CLK), .I(MAR_I));
  Byte_Reg MBR (
    .Chip_Select(control_unit_1_mbr_cs), .Clock(CLK), .Mode_RW(control_unit_1_mbr_rw), .O(MBR_I), .I(MBR_I));
  Byte_Reg D0 (
    .Chip_Select(control_unit_1_d0_rw[1]), .Clock(CLK), .Mode_RW(control_unit_1_d0_rw[0]), .O(D0_o), .I(D0_o));
  Byte_Reg D1 (
    .Chip_Select(control_unit_1_d0_rw[3]), .Clock(CLK), .Mode_RW(control_unit_1_d0_rw[2]), .O(D0_o), .I(D0_o));
  assign MAR_I = MBR_I[3:0];  // Buffer buffer_1, 4 bits wide
  ALU alu_1 (
    .A(D0_o), .R(D0_o), .L(D0_o), .ADD_SUB(control_unit_1_alu_add_sub), .CLK(CLK),
    .CTRL(control_unit_1_alu_ctrl));  // open: Status
  Nibble_Counter IC (
    .Write_Enable(control_unit_1_ic_ctrl[0]), .I(MAR_I), .Increment(control_unit_1_ic_ctrl[2]),
    .Read_Enable(control_unit_1_ic_ctrl[1]), .Clock(CLK), .O(MAR_I));
  Byte_Reg IR (.Chip_Select(control_unit_1_ir_cs), .Clock(CLK), .Mode_RW(control_unit_1_ir_rw), .O(IR_o), .I(MBR_I));
  Control_Unit control_unit_1 (
    .EXT_CTRL(EXT_CTRL), .OP(IR_o), .D0_CS(control_unit_1_d0_rw[1]), .D0_RW(control_unit_1_d0_rw[0]),
    .D1_CS(control_unit_1_d0_rw[3]), .D1_RW(control_unit_1_d0_rw[2]), .ALU_CTRL(control_unit_1_alu_ctrl),
    .ALU_ADD_SUB(control_unit_1_alu_add_sub), .IC_CTRL(control_unit_1_ic_ctrl),
    .MAR_RW(control_unit_1_mar_rw), .MAR_CS(control_unit_1_mar_cs), .MBR_RW(control_unit_1_mbr_rw),
    .MBR_CS(control_unit_1_mbr_cs), .IR_RW(control_unit_1_ir_rw), .IR_CS(control_unit_1_ir_cs), .CLK(CLK));

  assign MAR_O = MAR_I;
  assign MBR_O = MBR_I;

  // Notes on the sheet:
  //   Fix byte length or spread over multiple pins
endmodule

module Control_Unit (
  input  [7:0] OP,
  input  CLK,
  output D0_RW,
  output D0_CS,
  output D1_RW,
  output D1_CS,
  output ALU_ADD_SUB,
  output [3:0] ALU_CTRL,
  output [2:0] IC_CTRL,
  output MAR_RW,
  output MAR_CS,
  output MBR_RW,
  output MBR_CS,
  output IR_RW,
  output IR_CS,
  output [5:0] EXT_CTRL
);

  wire and_1_out, and_2_out, and_3_out, and_4_out, and_5_out, or_1_out, or_2_out, or_3_out, or_4_out,
       or_6_out, or_9_out, or_10_out, or_11_out, or_14_out;

  or or_1 (or_1_out, ALU_CTRL[3], IC_CTRL[1]);
  T_Flip_Flop #(.trigger("falling")) t_ff_1 (.T(or_1_out), .clk(CLK), .Q(IC_CTRL[1]));  // open: Qn, reset, preset
  or or_2 (or_2_out, IC_CTRL[1], EXT_CTRL[0]);
  T_Flip_Flop #(.trigger("falling")) t_ff_2 (.T(or_2_out), .clk(CLK), .Q(EXT_CTRL[0]));  // open: Qn, reset, preset
  not not_1 (EXT_CTRL[3], EXT_CTRL[0]);
  or or_3 (or_3_out, EXT_CTRL[0], EXT_CTRL[1]);
  T_Flip_Flop #(.trigger("falling")) t_ff_3 (.T(or_3_out), .clk(CLK), .Q(EXT_CTRL[1]));  // open: Qn, reset, preset
  or or_4 (or_4_out, EXT_CTRL[1], EXT_CTRL[2]);
  T_Flip_Flop #(.trigger("falling")) t_ff_4 (.T(or_4_out), .clk(CLK), .Q(EXT_CTRL[2]));  // open: Qn, reset, preset
  and and_1 (and_1_out, OP[4], OP[5], ~OP[6], ~OP[7]);  // AND_Gate
  or or_5 (ALU_ADD_SUB, and_1_out, OP[7]);
  or or_6 (or_6_out, EXT_CTRL[2], IR_RW);
  T_Flip_Flop #(.trigger("falling")) t_ff_5 (.T(or_6_out), .clk(CLK), .Q(IR_RW));  // open: Qn, reset, preset
  or or_7 (MAR_CS, IC_CTRL[1], EXT_CTRL[0], IR_RW);
  or or_8 (MBR_CS, EXT_CTRL[2], IR_RW);
  or or_9 (or_9_out, IR_RW, ALU_CTRL[0]);
  T_Flip_Flop #(.trigger("falling")) t_ff_6 (.T(or_9_out), .clk(CLK), .Q(ALU_CTRL[0]));  // open: Qn, reset, preset
  and and_2 (and_2_out, ~OP[4], ALU_CTRL[0]);  // AND_Gate
  and and_3 (and_3_out, ALU_CTRL[0], OP[4]);
  or or_10 (or_10_out, ALU_CTRL[0], ALU_CTRL[1]);
  T_Flip_Flop #(.trigger("falling")) t_ff_7 (.T(or_10_out), .clk(CLK), .Q(ALU_CTRL[1]));  // open: Qn, reset, preset
  and and_4 (and_4_out, ~OP[5], ALU_CTRL[1]);  // AND_Gate
  and and_5 (and_5_out, ALU_CTRL[1], OP[5]);
  or or_11 (or_11_out, ALU_CTRL[1], ALU_CTRL[2]);
  T_Flip_Flop #(.trigger("falling")) t_ff_8 (.T(or_11_out), .clk(CLK), .Q(ALU_CTRL[2]));  // open: Qn, reset, preset
  or or_12 (D0_CS, and_2_out, and_4_out);
  or or_13 (D1_CS, and_5_out, and_3_out);
  or or_14 (or_14_out, ALU_CTRL[2], ALU_CTRL[3]);
  T_Flip_Flop #(.trigger("falling")) t_ff_9 (.T(or_14_out), .clk(CLK), .Q(ALU_CTRL[3]));  // open: Qn, reset, preset
  or or_15 (IR_CS, IR_RW, ALU_CTRL[0], ALU_CTRL[1], ALU_CTRL[2], ALU_CTRL[3]);

  assign IC_CTRL[2] = EXT_CTRL[1];
  assign MAR_RW = IC_CTRL[1];
  assign MBR_RW = EXT_CTRL[2];

  // Notes on the sheet:
  //   Probably can reduce, depends on your instructions
  //   IC to MAR
  //   RAM - Read at MAR
  //   RAM Exec & IC ++
  //   RAM D to MBR
  //   MBR to IR AND MAR
  //   Main Step 1
  //   Main Step 2
  //   Main Step 3
  //   Main Step 4
  //   OUT, IN, RAM M, RAM F, RAM E, RAM S
  //   INC, R, W
  //   OUT, EXEC, R_IN, L_IN
endmodule

module Binary_to_BCD (
  input  [7:0] BInaryInput,
  output [3:0] Binary1,
  output [3:0] Binary10,
  output [3:0] Binary100
);

  wire [2:0] add3_5_out_2;
  wire [3:0] add3_1_out_2, add3_2_out_2, add3_3_out_2, add3_4_out_2;

  Add3 add3_1 (.out_2(add3_1_out_2), .in_1({1'b0, BInaryInput[7:5]}));
  Add3 add3_2 (.out_2(add3_2_out_2), .in_1({add3_1_out_2[2:0], BInaryInput[4]}));
  Add3 add3_3 (.out_2(add3_3_out_2), .in_1({add3_2_out_2[2:0], BInaryInput[3]}));
  Add3 add3_4 (.out_2(add3_4_out_2), .in_1({add3_3_out_2[2:0], BInaryInput[2]}));
  Add3 add3_5 (.out_2({Binary100[1], add3_5_out_2}), .in_1({1'b0, add3_1_out_2[3], add3_2_out_2[3], add3_3_out_2[3]}));
  Add3 add3_6 (.out_2({Binary10[0], Binary1[3:1]}), .in_1({add3_4_out_2[2:0], BInaryInput[1]}));
  Add3 add3_7 (.out_2({Binary100[0], Binary10[3:1]}), .in_1({add3_5_out_2, add3_4_out_2[3]}));

  assign Binary1[0] = BInaryInput[0];
  assign Binary100[3:2] = 2'b00;
endmodule

module BCD_to_7Segment (
  input  [3:0] in_1,
  output [6:0] out_2
);

  wire and_1_out, and_2_out, and_3_out, and_4_out, and_5_out, and_6_out, and_7_out, and_8_out, and_9_out,
       and_10_out, and_11_out, and_12_out, and_14_out, not_1_out, not_2_out, not_3_out, not_4_out, or_1_out,
       or_2_out, or_3_out, xor_1_out, xor_2_out;

  not not_1 (not_1_out, in_1[3]);
  not not_2 (not_2_out, in_1[2]);
  not not_3 (not_3_out, in_1[1]);
  not not_4 (not_4_out, in_1[0]);
  and and_1 (and_1_out, in_1[0], not_3_out, not_2_out, not_1_out);
  and and_2 (and_2_out, not_4_out, not_3_out, in_1[2], not_1_out);
  and and_3 (and_3_out, in_1[2], not_1_out);
  xor xor_1 (xor_1_out, in_1[0], in_1[1]);
  nand nand_1 (out_2[4], not_4_out, in_1[1], not_2_out, not_1_out);
  xor xor_2 (xor_2_out, in_1[0], in_1[2]);
  and and_4 (and_4_out, xor_2_out, not_3_out);
  and and_5 (and_5_out, in_1[0], in_1[1], in_1[2]);
  and and_6 (and_6_out, in_1[1], not_2_out, not_1_out);
  and and_7 (and_7_out, in_1[1], in_1[2], not_1_out);
  or or_1 (or_1_out, and_6_out, and_7_out, and_8_out, and_9_out);
  and and_8 (and_8_out, not_3_out, not_2_out, in_1[3]);
  and and_9 (and_9_out, not_3_out, not_2_out, not_1_out);
  and and_10 (and_10_out, not_1_out, not_2_out);
  or or_2 (or_2_out, in_1[0], in_1[1]);
  and and_11 (and_11_out, in_1[0], in_1[1], in_1[2], not_1_out);
  and and_12 (and_12_out, not_3_out, not_2_out, not_1_out);
  and and_13 (out_2[2], ~and_1_out, ~and_2_out);  // AND_Gate
  nand nand_2 (out_2[3], and_3_out, xor_1_out);
  or or_3 (or_3_out, and_4_out, and_5_out);
  and and_14 (and_14_out, and_10_out, or_2_out);
  nand nand_3 (out_2[5], not_1_out, or_3_out);
  and and_15 (out_2[6], not_4_out, or_1_out);
  nor nor_1 (out_2[1], and_14_out, and_11_out);
  nor nor_2 (out_2[0], and_11_out, and_12_out);

  // Notes on the sheet:
  //   Segment order: GFABCDE
endmodule

module RAM_16x8 (
  input  CLK,
  input  Mode,
  input  [3:0] Address,
  input  [2:0] CPU_CTRL,
  input  [7:0] Data_in,
  output [7:0] Data_out
);

  wire and_1_out, controlled_buffer_1_out, d_ff_1_q, d_ff_1_qn, decoder_1_out0, decoder_1_out1,
       decoder_1_out2, decoder_1_out3, decoder_1_out4, decoder_1_out5, decoder_1_out6, decoder_1_out7,
       decoder_1_out8, decoder_1_out9, decoder_1_out10, decoder_1_out11, decoder_1_out12, decoder_1_out13,
       decoder_1_out14, decoder_1_out15, not_1_out, not_2_out, or_1_out;
  wire [3:0] nibble_reg_1_o;
  wire [7:0] D_o, demultiplexer_1_out0, multiplexer_1_out, R_0_o;

  Byte_Reg R_0 (.Chip_Select(decoder_1_out0), .Clock(CLK), .Mode_RW(d_ff_1_q), .O(R_0_o), .I(demultiplexer_1_out0));
  Byte_Reg R_4 (.Chip_Select(decoder_1_out4), .Clock(CLK), .Mode_RW(d_ff_1_q), .O(R_0_o), .I(demultiplexer_1_out0));
  Byte_Reg R_8 (.Chip_Select(decoder_1_out8), .Clock(CLK), .Mode_RW(d_ff_1_q), .O(R_0_o), .I(demultiplexer_1_out0));
  Byte_Reg R_12 (.Chip_Select(decoder_1_out12), .Clock(CLK), .Mode_RW(d_ff_1_q), .O(R_0_o), .I(demultiplexer_1_out0));
  // Probe on R_0_o
  Multiplexer #(.width(8), .enable("false")) multiplexer_1 (
    .in0(R_0_o), .in1(Data_in), .out(multiplexer_1_out), .sel(CPU_CTRL[0]));
  Byte_Reg R_1 (.Chip_Select(decoder_1_out1), .Clock(CLK), .Mode_RW(d_ff_1_q), .O(R_0_o), .I(demultiplexer_1_out0));
  Byte_Reg R_5 (.Chip_Select(decoder_1_out5), .Clock(CLK), .Mode_RW(d_ff_1_q), .O(R_0_o), .I(demultiplexer_1_out0));
  Byte_Reg R_9 (.Chip_Select(decoder_1_out9), .Clock(CLK), .Mode_RW(d_ff_1_q), .O(R_0_o), .I(demultiplexer_1_out0));
  Byte_Reg R_13 (.Chip_Select(decoder_1_out13), .Clock(CLK), .Mode_RW(d_ff_1_q), .O(R_0_o), .I(demultiplexer_1_out0));
  or or_1 (or_1_out, CPU_CTRL[0], and_1_out);
  // Probe on multiplexer_1_out
  not not_1 (not_1_out, CLK);
  not not_2 (not_2_out, not_1_out);
  Byte_Reg D (.Chip_Select(1'b1), .Clock(not_2_out), .Mode_RW(or_1_out), .O(D_o), .I(multiplexer_1_out));
  // Probe on D_o
  Byte_Reg R_2 (.Chip_Select(decoder_1_out2), .Clock(CLK), .Mode_RW(d_ff_1_q), .O(R_0_o), .I(demultiplexer_1_out0));
  Byte_Reg R_6 (.Chip_Select(decoder_1_out6), .Clock(CLK), .Mode_RW(d_ff_1_q), .O(R_0_o), .I(demultiplexer_1_out0));
  Byte_Reg R_10 (.Chip_Select(decoder_1_out10), .Clock(CLK), .Mode_RW(d_ff_1_q), .O(R_0_o), .I(demultiplexer_1_out0));
  Byte_Reg R_14 (.Chip_Select(decoder_1_out14), .Clock(CLK), .Mode_RW(d_ff_1_q), .O(R_0_o), .I(demultiplexer_1_out0));
  Demultiplexer #(.width(8), .enable("false")) demultiplexer_1 (
    .out0(demultiplexer_1_out0), .out1(Data_out), .in(D_o), .sel(CPU_CTRL[2]));
  Byte_Reg R_3 (.Chip_Select(decoder_1_out3), .Clock(CLK), .Mode_RW(d_ff_1_q), .O(R_0_o), .I(demultiplexer_1_out0));
  Byte_Reg R_7 (.Chip_Select(decoder_1_out7), .Clock(CLK), .Mode_RW(d_ff_1_q), .O(R_0_o), .I(demultiplexer_1_out0));
  Byte_Reg R_11 (.Chip_Select(decoder_1_out11), .Clock(CLK), .Mode_RW(d_ff_1_q), .O(R_0_o), .I(demultiplexer_1_out0));
  Byte_Reg R_15 (.Chip_Select(decoder_1_out15), .Clock(CLK), .Mode_RW(d_ff_1_q), .O(R_0_o), .I(demultiplexer_1_out0));
  Decoder #(.select(4), .enable("false")) decoder_1 (
    .out0(decoder_1_out0), .out1(decoder_1_out1), .out2(decoder_1_out2), .out3(decoder_1_out3),
    .out4(decoder_1_out4), .out5(decoder_1_out5), .out6(decoder_1_out6), .out7(decoder_1_out7),
    .out8(decoder_1_out8), .out9(decoder_1_out9), .out10(decoder_1_out10), .out11(decoder_1_out11),
    .out12(decoder_1_out12), .out13(decoder_1_out13), .out14(decoder_1_out14), .out15(decoder_1_out15),
    .sel(nibble_reg_1_o));
  and and_1 (and_1_out, CPU_CTRL[1], d_ff_1_qn);
  D_Flip_Flop d_ff_1 (.D(Mode), .clk(controlled_buffer_1_out), .Q(d_ff_1_q), .Qn(d_ff_1_qn));  // open: preset, reset
  assign controlled_buffer_1_out = CPU_CTRL[0] ? CLK : 1'bz;  // Controlled_Buffer controlled_buffer_1
  Nibble_Reg nibble_reg_1 (.O(nibble_reg_1_o), .Chip_Select(1'b1), .Mode_RW(CPU_CTRL[0]), .Clock(CLK), .I(Address));

  // Other names for the same wires on the sheet: SET = CPU_CTRL[0]; EXEC = CPU_CTRL[1]; FETCH = CPU_CTRL[2]

  // Notes on the sheet:
  //   FETCH, EXEC, SET
endmodule

module ALU (
  input  [3:0] CTRL,
  input  ADD_SUB,
  input  CLK,
  input  [7:0] L,
  input  [7:0] R,
  output [2:0] Status,
  output [7:0] A
);

  wire or_1_out, or_2_out, or_3_out, or_4_out;
  wire [3:0] undriven;
  wire [3:3] nibble_reg_1_o;
  wire [7:0] byte_reg_1_o, byte_reg_2_o, nor_1_out, S_out, xor_1_out;
  wire [7:1] Cout_out;
  wire [7:7] Cout_out_2;

  or or_1 (or_1_out, CTRL[2], CTRL[0]);
  or or_2 (or_2_out, CTRL[2], CTRL[1]);
  Byte_Reg byte_reg_1 (.Chip_Select(or_1_out), .Clock(CLK), .Mode_RW(CTRL[0]), .O(byte_reg_1_o), .I(L));
  Byte_Reg byte_reg_2 (.Chip_Select(or_2_out), .Clock(CLK), .Mode_RW(CTRL[1]), .O(byte_reg_2_o), .I(R));
  assign xor_1_out = {8{ADD_SUB}} ^ byte_reg_1_o;  // XOR_Gate xor_1, 8 bits wide
  assign S_out = xor_1_out ^ byte_reg_2_o ^ {Cout_out, ADD_SUB};  // XOR_Gate S, 8 bits wide
  NotExactlyOne Cout[7:0] (
    .out({Cout_out_2[7], Cout_out}), .in0(byte_reg_2_o), .in1(xor_1_out), .in2({Cout_out, ADD_SUB}),
    .in3(nor_1_out));
  assign nor_1_out = ~({Cout_out, ADD_SUB} | byte_reg_2_o | xor_1_out);  // NOR_Gate nor_1, 8 bits wide
  nor Zero (undriven[1], S_out[0], S_out[1], S_out[2], S_out[3], S_out[4], S_out[5], S_out[6], S_out[7]);
  or or_3 (or_3_out, CTRL[3], CTRL[2]);
  or or_4 (or_4_out, CTRL[3], CTRL[2]);
  Nibble_Reg nibble_reg_1 (
    .O({nibble_reg_1_o[3], Status}), .Chip_Select(or_3_out), .Mode_RW(CTRL[2]), .Clock(CLK),
    .I({undriven[3], Cout_out_2[7], undriven[1:0]}));
  Byte_Reg byte_reg_3 (.Chip_Select(or_4_out), .Clock(CLK), .Mode_RW(CTRL[2]), .O(A), .I(S_out));

  // Other names for the same wires on the sheet: L_IN = CTRL[0]; R_IN = CTRL[1]; EXEC = CTRL[2]; A_OUT = CTRL[3]

  // Notes on the sheet:
  //   ALU operations: Add, Sub, Compare = Sub
  //   OUT, EXEC, R_IN, L_IN
  //   Neg, Zero, OF
endmodule

module Byte_Reg (
  input  [7:0] I,
  input  Clock,
  input  Mode_RW,
  input  Chip_Select,
  output [7:0] O
);

  wire and_1_out, and_2_out, not_1_out, not_2_out;
  wire [7:0] controlled_buffer_1_out, R_0_q;

  not not_1 (not_1_out, Clock);
  assign controlled_buffer_1_out = and_1_out ? I : 8'bz;  // Controlled_Buffer controlled_buffer_1
  not not_2 (not_2_out, not_1_out);
  and and_1 (and_1_out, Mode_RW, Chip_Select);
  and and_2 (and_2_out, Chip_Select, ~Mode_RW);  // AND_Gate
  D_Flip_Flop R_4 (.D(controlled_buffer_1_out[4]), .clk(not_2_out), .Q(R_0_q[4]));  // open: Qn, preset, reset
  D_Flip_Flop R_5 (.D(controlled_buffer_1_out[5]), .clk(not_2_out), .Q(R_0_q[5]));  // open: Qn, preset, reset
  D_Flip_Flop R_6 (.D(controlled_buffer_1_out[6]), .clk(not_2_out), .Q(R_0_q[6]));  // open: Qn, preset, reset
  D_Flip_Flop R_7 (.D(controlled_buffer_1_out[7]), .clk(not_2_out), .Q(R_0_q[7]));  // open: Qn, preset, reset
  assign O = and_2_out ? R_0_q : 8'bz;  // Controlled_Buffer controlled_buffer_2
  D_Flip_Flop R_0 (.D(controlled_buffer_1_out[0]), .clk(not_2_out), .Q(R_0_q[0]));  // open: Qn, preset, reset
  D_Flip_Flop R_1 (.D(controlled_buffer_1_out[1]), .clk(not_2_out), .Q(R_0_q[1]));  // open: Qn, preset, reset
  D_Flip_Flop R_2 (.D(controlled_buffer_1_out[2]), .clk(not_2_out), .Q(R_0_q[2]));  // open: Qn, preset, reset
  D_Flip_Flop R_3 (.D(controlled_buffer_1_out[3]), .clk(not_2_out), .Q(R_0_q[3]));  // open: Qn, preset, reset
endmodule

module Nibble_Reg (
  input  [3:0] I,
  input  Clock,
  input  Mode_RW,
  input  Chip_Select,
  output [3:0] O
);

  wire and_1_out, and_2_out, not_1_out, not_2_out;
  wire [3:0] controlled_buffer_1_out, d_ff_1_q;

  not not_1 (not_1_out, Clock);
  assign controlled_buffer_1_out = and_1_out ? I : 4'bz;  // Controlled_Buffer controlled_buffer_1
  not not_2 (not_2_out, not_1_out);
  and and_1 (and_1_out, Mode_RW, Chip_Select);
  and and_2 (and_2_out, Chip_Select, ~Mode_RW);  // AND_Gate
  D_Flip_Flop d_ff_1 (.D(controlled_buffer_1_out[0]), .clk(not_2_out), .Q(d_ff_1_q[0]));  // open: Qn, preset, reset
  D_Flip_Flop d_ff_2 (.D(controlled_buffer_1_out[1]), .clk(not_2_out), .Q(d_ff_1_q[1]));  // open: Qn, preset, reset
  D_Flip_Flop d_ff_3 (.D(controlled_buffer_1_out[2]), .clk(not_2_out), .Q(d_ff_1_q[2]));  // open: Qn, preset, reset
  D_Flip_Flop d_ff_4 (.D(controlled_buffer_1_out[3]), .clk(not_2_out), .Q(d_ff_1_q[3]));  // open: Qn, preset, reset
  assign O = and_2_out ? d_ff_1_q : 4'bz;  // Controlled_Buffer controlled_buffer_2
endmodule

module Nibble_Counter (
  input  [3:0] I,
  input  Write_Enable,
  input  Increment,
  input  Read_Enable,
  input  Clock,
  output [3:0] O
);

  wire and_1_out, and_2_out, and_3_out, or_1_out, or_2_out, or_3_out, or_4_out, or_5_out, or_6_out, or_7_out,
       or_8_out;
  wire [3:0] controlled_buffer_1_out, j_k_ff_1_q;

  assign controlled_buffer_1_out = Write_Enable ? I : 4'bz;  // Controlled_Buffer controlled_buffer_1
  or or_1 (or_1_out, controlled_buffer_1_out[0], Increment);
  or or_2 (or_2_out, Increment, ~controlled_buffer_1_out[0]);  // OR_Gate
  and and_1 (and_1_out, j_k_ff_1_q[0], Increment);
  J_K_Flip_Flop j_k_ff_1 (.J(or_1_out), .K(or_2_out), .clk(Clock), .Q(j_k_ff_1_q[0]));  // open: Qn, preset, reset
  J_K_Flip_Flop j_k_ff_2 (.J(or_3_out), .K(or_4_out), .clk(Clock), .Q(j_k_ff_1_q[1]));  // open: Qn, preset, reset
  or or_3 (or_3_out, controlled_buffer_1_out[1], and_1_out);
  or or_4 (or_4_out, and_1_out, ~controlled_buffer_1_out[1]);  // OR_Gate
  and and_2 (and_2_out, j_k_ff_1_q[1], j_k_ff_1_q[0], Increment);
  or or_5 (or_5_out, controlled_buffer_1_out[2], and_2_out);
  or or_6 (or_6_out, and_2_out, ~controlled_buffer_1_out[2]);  // OR_Gate
  J_K_Flip_Flop j_k_ff_3 (.J(or_5_out), .K(or_6_out), .clk(Clock), .Q(j_k_ff_1_q[2]));  // open: Qn, preset, reset
  and and_3 (and_3_out, j_k_ff_1_q[2], j_k_ff_1_q[1], j_k_ff_1_q[0], Increment);
  J_K_Flip_Flop j_k_ff_4 (.J(or_7_out), .K(or_8_out), .clk(Clock), .Q(j_k_ff_1_q[3]));  // open: Qn, preset, reset
  or or_7 (or_7_out, controlled_buffer_1_out[3], and_3_out);
  or or_8 (or_8_out, and_3_out, ~controlled_buffer_1_out[3]);  // OR_Gate
  assign O = Read_Enable ? j_k_ff_1_q : 4'bz;  // Controlled_Buffer controlled_buffer_2
endmodule

module Bit_Adder (
  input  Cin,
  input  X,
  input  Y,
  output Sum,
  output Cout
);

  wire and_1_out, and_2_out, xor_1_out;

  and and_1 (and_1_out, Y, X);
  or or_1 (Cout, and_1_out, and_2_out);
  xor xor_1 (xor_1_out, X, Y);
  and and_2 (and_2_out, xor_1_out, Cin);
  xor xor_2 (Sum, Cin, xor_1_out);
endmodule

module Add3 (
  input  [3:0] in_1,
  output [3:0] out_2
);

  wire and_1_out, and_2_out, and_3_out, and_4_out, and_5_out, and_6_out, and_7_out, and_8_out, and_9_out,
       bit_adder_1_cout, bit_adder_1_sum, bit_adder_2_cout, bit_adder_2_sum, bit_adder_3_cout,
       bit_adder_3_sum, bit_adder_4_sum, or_1_out, or_2_out;

  or or_1 (or_1_out, in_1[0], in_1[1]);
  and and_1 (and_1_out, or_1_out, in_1[2]);
  Bit_Adder bit_adder_1 (.Cout(bit_adder_1_cout), .Sum(bit_adder_1_sum), .Y(1'b1), .X(in_1[0]));  // open: Cin
  Bit_Adder bit_adder_2 (.Cout(bit_adder_2_cout), .Sum(bit_adder_2_sum), .Y(1'b1), .X(in_1[1]), .Cin(bit_adder_1_cout));
  Bit_Adder bit_adder_3 (.Cout(bit_adder_3_cout), .Sum(bit_adder_3_sum), .Y(1'b0), .X(in_1[2]), .Cin(bit_adder_2_cout));
  Bit_Adder bit_adder_4 (.Sum(bit_adder_4_sum), .Y(1'b0), .X(in_1[3]), .Cin(bit_adder_3_cout));  // open: Cout
  or or_2 (or_2_out, in_1[3], and_1_out);
  and and_2 (and_2_out, or_2_out, bit_adder_1_sum);
  and and_3 (and_3_out, ~or_2_out, in_1[0]);  // AND_Gate
  and and_4 (and_4_out, or_2_out, bit_adder_2_sum);
  and and_5 (and_5_out, ~or_2_out, in_1[1]);  // AND_Gate
  and and_6 (and_6_out, or_2_out, bit_adder_3_sum);
  and and_7 (and_7_out, ~or_2_out, in_1[2]);  // AND_Gate
  and and_8 (and_8_out, or_2_out, bit_adder_4_sum);
  and and_9 (and_9_out, ~or_2_out, in_1[3]);  // AND_Gate
  or or_3 (out_2[0], and_2_out, and_3_out);
  or or_4 (out_2[1], and_4_out, and_5_out);
  or or_5 (out_2[2], and_6_out, and_7_out);
  or or_6 (out_2[3], and_8_out, and_9_out);
endmodule
